# Fritzing sketch circuit (saved by Fritzing 0.9.9b)

parts:
  Arduino = Arduino Uno (Rev3)
  MAX7219 = MAX7219 [package=dil24]

nets:
  GND: Arduino.GND, MAX7219.GND
  N1: Arduino.D5_PWM, MAX7219.CLK
  N2: Arduino.D6_PWM, MAX7219.CS
  N3: Arduino.D7, MAX7219.DIN
  5V: Arduino.5V, MAX7219.VCC

custom parts:
  MAX7219: 8-digit, 8-segment LED display driver, serial input
