# Fritzing sketch circuit (saved by Fritzing 0.9.9b)

parts:
  Arduino = Arduino Uno (Rev3)
  J1 = Basic Servo

nets:
  GND: Arduino.GND, J1.gnd
  N1: Arduino.D6_PWM, J1.pulse
  5V: Arduino.5V, J1.vcc
