# Fritzing sketch circuit (saved by Fritzing 0.9.9b)
breadboards: 1

parts:
  R1 = Resistor [tolerance=±5% power=0.25 resistance=330 package=THT]
  S1 = Pushbutton [package="[THT]"]
  S2 = Pushbutton [package="[THT]"]
  LED1 = LED - 5mm [color="Red (633nm)" current=0.030 package="5 mm [THT]"]
  Arduino = Arduino Uno (Rev3)

nets:
  N1: R1.Pin_0, LED1.anode
  N2: R1.Pin_1, Arduino.D8
  N3: S1.Pin_1, S1.Pin_2, Arduino.D4
  N4: S1.Pin_3, S1.Pin_4, S2.Pin_3, S2.Pin_4, LED1.cathode, Arduino.GND
  N5: S2.Pin_1, S2.Pin_2, Arduino.D2
