# Fritzing sketch circuit (saved by Fritzing 0.9.9b)
breadboards: 1

parts:
  Arduino = Arduino Uno (Rev3)
  LED1 = LED - 5mm [color="Red (633nm)" current=0.030 package="5 mm [THT]"]
  R1 = Resistor [tolerance=±5% power=0.25 resistance=330 package=THT]
  S1 = Pushbutton [package="[THT]"]
  S2 = Pushbutton [package="[THT]"]

nets:
  N1: Arduino.D8, R1.Pin_1
  N2: Arduino.GND, LED1.cathode
  N3: Arduino.D2, S2.Pin_1, S2.Pin_2
  N4: Arduino.D4, S1.Pin_1, S1.Pin_2
  N5: Arduino.5V, S1.Pin_3, S1.Pin_4, S2.Pin_3, S2.Pin_4
  N6: LED1.anode, R1.Pin_0
