# Fritzing sketch circuit (saved by Fritzing 0.9.9b)
breadboards: 1

parts:
  Arduino = Arduino Uno (Rev3)
  S1 = Round Pushbutton
  U1 = ENCODER-QUADRATURE [package=encoder-16mm-quad]

nets:
  N1: Arduino.D8, U1.C
  N2: Arduino.D9_PWM, U1.A
  N3: Arduino.D12/MISO, S1.leg0
  N4: Arduino.GND, S1.leg1, U1.B
