# Fritzing sketch circuit (saved by Fritzing 0.9.9b)

parts:
  Arduino = Arduino Uno (Rev3)
  R1 = Rotary Potentiometer (Large) [maximum_resistance=100kΩ package=THT]

nets:
  N1: Arduino.D8, R1.wiper
  N2: Arduino.GND, R1.leg1
  N3: Arduino.5V, R1.leg2
